# Fritzing sketch signalrpi (saved by Fritzing 1.0.8)
perfboards: 1

parts:
  Mod1 = Raspberry Pi Pico W
  U1 = CC1101 [part_number=CC1101]
  M1 = cc1101 module
  C1 = Electrolytic Capacitor [capacitance=100µF voltage=10V package="100 mil [THT, electrolytic]"]
  C2 = Ceramic Capacitor [capacitance=10µF voltage=35V package="100 mil [THT, multilayer]"]
  C3 = Ceramic Capacitor [capacitance=10µF voltage=35V package="100 mil [THT, multilayer]"]

nets:
  GND: Mod1.pin_8, Mod1.pin_33, U1.2, M1.pin_9, M1.pin_10, C1.-, C2.0, C3.0
  N1: Mod1.pin_9, M1.pin_8
  N2: Mod1.pin_14, M1.pin_4
  N3: Mod1.pin_15, M1.pin_3
  N4: Mod1.pin_16, M1.pin_5
  N5: Mod1.pin_17, M1.pin_7
  N6: Mod1.pin_21, U1.5
  N7: Mod1.pin_22, U1.8
  N8: Mod1.pin_24, U1.4
  N9: Mod1.pin_25, U1.3
  N10: Mod1.pin_26, U1.7
  N11: Mod1.pin_36, U1.1, M1.pin_1, M1.pin_2, C1.+, C2.1, C3.1

custom parts:
  Raspberry Pi Pico W: Raspberry Pi Pico W. Based around the RP2040 microcontroller the Pico W is a low cost microcontroller device bringing Raspberry Pi quality, cost, and easy of use to the microcontroller space. The areas marked KEEPOUT in pcb silkscreen should not have traces running through them to avoid shorts on a soldered in module!
  cc1101 module: CC1101 rf module.
